// Logisim project 디논.circ as structural Verilog: 1 circuit, main circuit main
module main (
  input  X,
  input  Y,
  output S,
  output C,
  output Q
);

  wire and_1_out, and_2_out, Clock_out, xor_1_out;

  and and_1 (and_1_out, X, Y);
  Clock Clock (.out(Clock_out));
  xor xor_1 (xor_1_out, X, Y);
  D_Flip_Flop \D_플립플롭  (.clk(Clock_out), .D(C), .Q(Q));  // open: Qn, preset, en, reset
  xor xor_2 (S, xor_1_out, Q);
  and and_2 (and_2_out, xor_1_out, Q);
  or or_1 (C, and_2_out, and_1_out);
endmodule
